// Logisim project 1_counter.circ as structural Verilog: 3 circuits, main circuit main
module main (
  input  start,
  input  clk,
  input  [7:0] in_3
);

  wire control_unit_1_clrr2, control_unit_1_clrr3, control_unit_1_incr2, control_unit_1_incr3,
       control_unit_1_shiftrightr1, datapath_unit_1_checklsb, datapath_unit_1_ready;
  wire [7:0] datapath_unit_1_answer, datapath_unit_1_r1_output, datapath_unit_1_r3_output;

  control_unit control_unit_1 (
    .incR2(control_unit_1_incr2), .clrR2(control_unit_1_clrr2), .start(start),
    .checkLSB(datapath_unit_1_checklsb), .ready(datapath_unit_1_ready), .clk(clk),
    .clrR3(control_unit_1_clrr3), .incR3(control_unit_1_incr3), .shiftRightR1(control_unit_1_shiftrightr1));
  datapath_unit datapath_unit_1 (
    .R1_output(datapath_unit_1_r1_output), .checkLSB(datapath_unit_1_checklsb), .clk(clk),
    .input0_shift1(start), .input_number(in_3), .shiftRightR1(control_unit_1_shiftrightr1),
    .incR3(control_unit_1_incr3), .incR2(control_unit_1_incr2), .clrR3(control_unit_1_clrr3),
    .clrR2(control_unit_1_clrr2), .Answer(datapath_unit_1_answer), .R3_output(datapath_unit_1_r3_output),
    .ready(datapath_unit_1_ready));
  // Probe on datapath_unit_1_r1_output
  // Probe on datapath_unit_1_answer
  // Probe on datapath_unit_1_r3_output
  // Probe on datapath_unit_1_ready
endmodule

module control_unit (
  input  checkLSB,
  input  ready,
  input  start,
  input  clk,
  output clrR2,
  output clrR3,
  output incR2,
  output incR3,
  output shiftRightR1
);

  wire and_5_out, and_6_out, and_7_out, and_8_out, and_9_out, and_10_out, and_11_out, g0, g1, g2, ncheckLSB,
       ng0, ng1, ng2, nready, nstart, or_1_out, or_2_out, or_3_out;

  not not_1 (ncheckLSB, checkLSB);
  not not_2 (nready, ready);
  not not_3 (nstart, start);
  and and_1 (clrR2, g0, ng1, start, ng2, nready);
  and and_2 (incR2, ng0, g1, ng2, checkLSB);
  and and_3 (incR3, ng0, g1, ng2);
  and and_4 (shiftRightR1, ng0, ng1, g2, nready);
  and and_5 (and_5_out, start, ready);
  or or_1 (or_1_out, and_5_out, nstart);
  and and_6 (and_6_out, or_1_out, ng2, ng1, g0);
  and and_7 (and_7_out, ng0, ng1, g2, ready);
  and and_8 (and_8_out, ng0, g1, g2);
  and and_9 (and_9_out, start, ng2, ng1, g0);
  or or_2 (or_2_out, and_6_out, and_7_out);
  or or_3 (or_3_out, and_8_out, and_9_out);
  D_Flip_Flop u_g0 (.D(or_2_out), .clk(clk), .Q(g0), .Qn(ng0));  // open: preset, reset
  and and_10 (and_10_out, nready, or_3_out);
  D_Flip_Flop u_g1 (.D(and_10_out), .clk(clk), .Q(g1), .Qn(ng1));  // open: preset, reset
  D_Flip_Flop u_g2 (.D(and_11_out), .clk(clk), .Q(g2), .Qn(ng2));  // open: preset, reset
  and and_11 (and_11_out, g0, g1, ng2);

  assign clrR3 = clrR2;

  // Notes on the sheet:
  //   input signals/status signals
  //   control signals
endmodule

module datapath_unit (
  input  clrR2,
  input  clrR3,
  input  incR2,
  input  incR3,
  input  shiftRightR1,
  input  [7:0] input_number,
  input  input0_shift1,
  input  clk,
  output checkLSB,
  output [7:0] R1_output,
  output [7:0] Answer,
  output [7:0] R3_output,
  output ready
);

  wire and_1_out, and_2_out, and_3_out, not_1_out, or_1_out;
  wire [7:0] adder_1_out, adder_2_out, multiplexer_1_out, shifter_1_out;

  Multiplexer #(.width(8), .enable("false")) multiplexer_1 (
    .in0(input_number), .in1(shifter_1_out), .out(multiplexer_1_out), .sel(input0_shift1));
  and and_1 (and_1_out, incR2, clk);
  and and_2 (and_2_out, incR3, clk);
  not not_1 (not_1_out, input0_shift1);
  or or_1 (or_1_out, not_1_out, shiftRightR1);
  and and_3 (and_3_out, or_1_out, clk);
  Adder adder_1 (.a(Answer), .b(8'h1), .out(adder_1_out));  // open: cin, cout
  Adder adder_2 (.a(R3_output), .b(8'h1), .out(adder_2_out));  // open: cin, cout
  Register R1 (.D(multiplexer_1_out), .en(1'b1), .clk(and_3_out), .Q({R1_output[7:1], checkLSB}));  // open: clr
  Register R2 (.D(adder_1_out), .en(1'b1), .clk(and_1_out), .Q(Answer), .clr(clrR2));
  Register R3 (.D(adder_2_out), .en(1'b1), .clk(and_2_out), .Q(R3_output), .clr(clrR3));
  Shifter #(.shift("lr")) shifter_1 (.in({R1_output[7:1], checkLSB}), .\dist (3'b001), .out(shifter_1_out));
  control_unit control_unit_1 ();  // open: incR2, clrR2, start, checkLSB, ready, clk, clrR3, incR3, shiftRightR1

  assign R1_output[0] = checkLSB;
  assign ready = R3_output[3];
endmodule
