// Logisim project D_FF_counter.circ as structural Verilog: 1 circuit, main circuit main
module main (
  input  in_1,
  output [1:0] out_2
);

  wire and_1_out, and_2_out, d_ff_1_qn, d_ff_2_qn, or_1_out;

  and and_1 (and_1_out, out_2[1], d_ff_2_qn);
  and and_2 (and_2_out, d_ff_1_qn, out_2[0]);
  or or_1 (or_1_out, and_1_out, and_2_out);
  D_Flip_Flop d_ff_1 (.D(or_1_out), .clk(in_1), .Q(out_2[1]), .Qn(d_ff_1_qn));  // open: preset, reset
  D_Flip_Flop d_ff_2 (.D(d_ff_2_qn), .clk(in_1), .Q(out_2[0]), .Qn(d_ff_2_qn));  // open: preset, reset
endmodule
