// Logisim project compare.circ as structural Verilog: 2 circuits, main circuit main
module main (
  input  [2:0] A,
  input  [2:0] B,
  output equal,
  output greater,
  output lesser
);

  wire and_2_out, and_3_out, comp_1_p1, comp_1_p4, comp_2_p1, comp_2_p4, comp_3_p1, comp_3_p4, not_1_out,
       not_2_out;

  // comp comp_1: pin names not known; wires that end beside it: comp_1_p1, B[2], A[2], comp_1_p4
  and and_1 (equal, comp_1_p1, comp_2_p1, comp_3_p1);
  not not_1 (not_1_out, equal);
  // comp comp_2: pin names not known; wires that end beside it: comp_2_p1, B[1], A[1], comp_2_p4
  and and_2 (and_2_out, comp_1_p1, comp_2_p4);
  or or_1 (greater, comp_1_p4, and_2_out, and_3_out);
  not not_2 (not_2_out, greater);
  // comp comp_3: pin names not known; wires that end beside it: comp_3_p1, B[0], A[0], comp_3_p4
  and and_3 (and_3_out, comp_1_p1, comp_2_p1, comp_3_p4);
  and and_4 (lesser, not_1_out, not_2_out);
endmodule

module comp (
  input  a,
  input  b,
  output greater,
  output equal
);

  wire and_1_out, and_2_out, not_1_out, not_2_out;

  not not_1 (not_1_out, a);
  not not_2 (not_2_out, b);
  and and_1 (and_1_out, a, b);
  and and_2 (and_2_out, not_1_out, not_2_out);
  and and_3 (greater, a, not_2_out);
  or or_1 (equal, and_1_out, and_2_out);
endmodule
