// Logisim project evolution_D_FF.circ as structural Verilog: 5 circuits, main circuit main
module main (
  input  preset,
  input  data,
  input  clk,
  input  clear,
  output q
);

  flipflop_t flipflop_t_1 (.preset(preset), .data(data), .clk(clk), .clear(clear), .Q(q));
endmodule

module flipflop_t (
  input  preset,
  input  data,
  input  clk,
  input  clear,
  output Q
);

  wire latch_t_1_q, latch_t_2_qb, not_1_out;

  not not_1 (not_1_out, clk);
  latch_t latch_t_1 (.preset(preset), .data(data), .enable(not_1_out), .clear(clear), .Q(latch_t_1_q));  // open: Qb
  latch_t latch_t_2 (.preset(preset), .data(latch_t_1_q), .enable(clk), .clear(clear), .Q(Q), .Qb(latch_t_2_qb));
endmodule

module latch_t (
  input  preset,
  input  data,
  input  enable,
  input  clear,
  output Q,
  output Qb
);

  wire A_out, B_out, C_out, D_out, E_out;

  not E (E_out, data);
  not A (A_out, preset);
  nand C (C_out, data, enable);
  nand D (D_out, enable, E_out);
  not B (B_out, clear);
  nand nand_1 (Q, C_out, A_out, Qb);
  nand nand_2 (Qb, Q, B_out, D_out);
endmodule

module register_t (
  input  preset,
  input  clear,
  input  clk,
  input  load,
  input  in_5,
  output out_6
);

  wire multiplexer_1_out;

  Multiplexer #(.enable("false")) multiplexer_1 (.in0(out_6), .in1(in_5), .out(multiplexer_1_out), .sel(load));
  flipflop_t flipflop_t_1 (.preset(preset), .data(multiplexer_1_out), .clk(clk), .clear(clear), .Q(out_6));
endmodule

module eightBit_register (
  input  [1:0] in_1,
  input  in_2,
  input  in_3,
  input  in_4,
  input  [2:0] in_5,
  output [2:0] out_6
);

  RAM #(.addrWidth(2), .dataWidth(3), .databus("bibus")) ram_1 (
    .addr(in_1), .we(in_2), .oe(in_3), .clk(in_4), .din(in_5), .dout(out_6));
endmodule
